# Fritzing sketch railroad_crossing (saved by Fritzing 0.9.10b)
breadboards: 1

parts:
  부품1 = Arduino Uno (Rev3)
  M2 = fc-51 [package=THT]
  J1 = Basic Servo  # not connected
  J2 = Basic Servo
  VCC1 = Battery
  VCC2 = Battery

nets:
  N1: 부품1.D8, M2.pin1
  N2: 부품1.D7, J2.pulse
  N3: 부품1.3V3, M2.pin3
  5V: 부품1.5V, J2.vcc, VCC1.+, VCC2.+
  GND: 부품1.GND, M2.pin2, J2.gnd, VCC1.-, VCC2.-
